# Fritzing sketch OhmTest (saved by Fritzing 0.9.3b)
breadboards: 1

parts:
  Componente1 = Arduino Nano (Rev3.0)
  Componente2 = Arduino Color LCD Shield
  U1 = BNC [package=bnc]
  U2 = BNC [package=bnc]
  R1 = Resistor [tolerance=±5% resistance=1k package="2010 [SMD]"]

nets:
  N1: Componente1.RESET, Componente2.A4, Componente2.RESET
  GND: Componente1.GND, Componente2.GND, R1.Pin_0
  N2: Componente1.D2, Componente2.D2
  N3: Componente1.D3, Componente2.D3
  N4: Componente1.D4, Componente2.D4
  N5: Componente1.D5, Componente2.D5
  N6: Componente1.D6, Componente2.D6
  N7: Componente1.D7, Componente2.D7
  N8: Componente1.D8, Componente2.D8
  N9: Componente1.D9, Componente2.D9
  N10: Componente1.D10, Componente2.D10
  N11: Componente1.D11/MOSI, Componente2.D11
  N12: Componente1.D12/MISO, Componente2.D12
  5V: Componente1.5V, Componente2.5V, U2.OUT
  N13: Componente1.A7, U1.OUT, R1.Pin_1
  N14: Componente1.A3, Componente2.A3
  N15: Componente1.A2, Componente2.A2
  N16: Componente1.A1, Componente2.A1
  N17: Componente1.A0, Componente2.A0
  3V3: Componente1.3V3, Componente2.3.3V
  N18: Componente1.D13/SCK, Componente2.D13
